# Fritzing sketch bargraph (saved by Fritzing 0.6.3b)
breadboards: 1

parts:
  Arduino1 = Arduino
  S1 = Pushbutton [package="[THT]"]
  R1 = Resistor [tolerance=±5% resistance=220 package=THT]
  LED1 = LED - 5mm [color="Red (633nm)" package="5 mm [THT]"]
  LED2 = LED - 5mm [color="Red (633nm)" package="5 mm [THT]"]
  LED3 = LED - 5mm [color="Red (633nm)" package="5 mm [THT]"]
  LED4 = LED - 5mm [color="Red (633nm)" package="5 mm [THT]"]
  LED5 = LED - 5mm [color="Red (633nm)" package="5 mm [THT]"]
  LED6 = LED - 5mm [color="Red (633nm)" package="5 mm [THT]"]
  LED7 = LED - 5mm [color="Red (633nm)" package="5 mm [THT]"]
  LED8 = LED - 5mm [color="Red (633nm)" package="5 mm [THT]"]
  LED9 = LED - 5mm [color="Red (633nm)" package="5 mm [THT]"]
  LED10 = LED - 5mm [color="Red (633nm)" package="5 mm [THT]"]
  R2 = Resistor [tolerance=±5% resistance=220 package=THT]
  R3 = Resistor [tolerance=±5% resistance=220 package=THT]
  R4 = Resistor [tolerance=±5% resistance=220 package=THT]
  R5 = Resistor [tolerance=±5% resistance=220 package=THT]
  R6 = Resistor [tolerance=±5% resistance=220 package=THT]
  R7 = Resistor [tolerance=±5% resistance=220 package=THT]
  R8 = Resistor [tolerance=±5% resistance=220 package=THT]
  R9 = Resistor [tolerance=±5% resistance=220 package=THT]
  R10 = Resistor [tolerance=±5% resistance=220 package=THT]
  R11 = Resistor [tolerance=±5% resistance=220 package=THT]
  R12 = Resistor [tolerance=±5% resistance=220 package=THT]

nets:
  N1: Arduino1.D12, LED10.cathode
  N2: Arduino1.D11, LED8.cathode
  N3: Arduino1.D10, LED9.cathode
  N4: Arduino1.D9, LED7.cathode
  N5: Arduino1.D8, LED5.cathode
  N6: Arduino1.D7, LED6.cathode
  N7: Arduino1.D6, LED4.cathode
  N8: Arduino1.D5, LED3.cathode
  N9: Arduino1.D4, LED2.cathode
  N10: Arduino1.D3, LED1.cathode
  N11: Arduino1.D2, S1.Pin_3, S1.Pin_4, R1.Pin_1
  N12: Arduino1.+5V, S1.Pin_1, S1.Pin_2
  N13: Arduino1.GND, R1.Pin_0, R9.Pin_1, R10.Pin_1, R11.Pin_1, R12.Pin_1
  N14: LED1.anode, R10.Pin_0
  N15: LED2.anode, R11.Pin_0
  N16: LED3.anode, R9.Pin_0
  N17: LED4.anode, R8.Pin_0
  N18: LED5.anode, R5.Pin_0
  N19: LED6.anode, R6.Pin_0
  N20: LED7.anode, R4.Pin_0
  N21: LED8.anode, R7.Pin_0
  N22: LED9.anode, R3.Pin_0
  N23: LED10.anode, R2.Pin_0
  N24: R2.Pin_1, R3.Pin_1, R4.Pin_1, R5.Pin_1, R6.Pin_1, R7.Pin_1, R8.Pin_1
